# Fritzing sketch stacjaPogodowa (saved by Fritzing 0.9.3b)
breadboards: 2

parts:
  LCD1 = LCD screen
  S1 = Pushbutton [package="[THT]"]
  R1 = Trimmer Potentiometer [maximum_resistance=1kΩ package=THT]
  R2 = Resistor [tolerance=±5% resistance=10k package="0805 [SMD]"]
  Part3 = Adafruit BME280
  Raspberry_Pi_1 = Raspberry Pi 3 [part_number=RPI-3-V1.2]
  U1 = SUP500F [package=sup500f]
  J1 = Cobbler Plus Cable

nets:
  GND: LCD1.VSS, LCD1.R/W, R1.leg2, Part3.GND, U1.GND, J1.GND#24
  VDD: LCD1.VDD, R1.leg1, Part3.VIN, U1.VCC, J1.5.0V#1
  N1: LCD1.V0, R1.wiper
  N2: LCD1.RS, J1.#6
  N3: LCD1.E, J1.#19
  N4: LCD1.DB4, J1.#26
  N5: LCD1.DB5, J1.#16
  N6: LCD1.DB6, J1.#20
  N7: LCD1.DB7, J1.#21
  N8: LCD1.LED+, R2.Pin_1, J1.5.0V#3
  N9: LCD1.LED-, S1.Pin_3, S1.Pin_4, J1.GND#5
  N10: S1.Pin_1, S1.Pin_2, R2.Pin_0, J1.#13
  N11: Part3.SCK/SCL, J1.SCL
  N12: Part3.SDI/SDA, J1.SDA
  3V3: Raspberry_Pi_1.3v3, Raspberry_Pi_1.3V3, J1.3.3V#41, J1.3.3V#57
  N13: Raspberry_Pi_1.GPIO2, J1.GPIO_2
  N14: Raspberry_Pi_1.GPIO3, J1.GPIO_3
  N15: Raspberry_Pi_1.GIPO4, J1.GPIO_4
  N16: Raspberry_Pi_1.GND, J1.GND#46, J1.GND#49, J1.GND#54, J1.GND#60, J1.GND#65, J1.GND#70, J1.GND#74, J1.GND#79
  N17: Raspberry_Pi_1.GIPO17, J1.GPIO_17
  N18: Raspberry_Pi_1.GIPO27, J1.GPIO_27
  N19: Raspberry_Pi_1.GIPO22, J1.GPIO_22
  N20: Raspberry_Pi_1.GIPO10, J1.GPIO_10
  N21: Raspberry_Pi_1.GIPO9, J1.GPIO_9
  N22: Raspberry_Pi_1.GIPO11, J1.GPIO_11
  N23: Raspberry_Pi_1.ID_SD, J1.ID_SD
  N24: Raspberry_Pi_1.GIPO5, J1.GPIO_5
  N25: Raspberry_Pi_1.GIPO6, J1.GPIO_6
  N26: Raspberry_Pi_1.GIPO13, J1.GPIO_13
  N27: Raspberry_Pi_1.GIPO19, J1.GPIO_19
  N28: Raspberry_Pi_1.GIPO26, J1.GPIO_26
  N29: Raspberry_Pi_1.GIPO21, J1.GPIO_21
  N30: Raspberry_Pi_1.GIPO20, J1.GPIO_20
  N31: Raspberry_Pi_1.GIPO16, J1.GPIO_16
  N32: Raspberry_Pi_1.GIPO12, J1.GPIO_12
  N33: Raspberry_Pi_1.ID_SC, J1.ID_SC
  N34: Raspberry_Pi_1.GIPO7, J1.GPIO_7
  N35: Raspberry_Pi_1.GIPO8, J1.GPIO_8
  N36: Raspberry_Pi_1.GIPO25, J1.GPIO_25
  N37: Raspberry_Pi_1.GIPO24, J1.GPIO_24
  N38: Raspberry_Pi_1.GIPO23, J1.GPIO_23
  N39: Raspberry_Pi_1.GIPO18, J1.GPIO_18
  N40: Raspberry_Pi_1.GIPO15, J1.GPIO_15
  N41: Raspberry_Pi_1.GIPO14, J1.GPIO_14
  5V: Raspberry_Pi_1.5V, J1.5V
  N42: U1.RX-I, J1.TXD
  N43: U1.TX-O, J1.RXD

custom parts:
  Adafruit BME280: Bosch has stepped up their game with their new BME280 sensor, an environmental sensor with temperature, barometric pressure and humidity! This sensor is great for all sorts of weather/environmental sensing and can even be used in both I2C and SPI! This precision sensor from Bosch is the best low-cost sensing solution for measuring humidity with ±3% accuracy, barometric pressure with ±1 hPa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
  Cobbler Plus Cable: The Cobbler Plus is an add on prototyping board from Adafruit specifically designed for the Raspberry Pi B+ that can break out all those tasty power, GPIO, I2C and SPI pins from the 40-pin header onto a solderless breadboard. This set will make "cobbling together" prototypes with the Pi super easy. The Cobbler Plus can plug into any solderless breadboard.
